# Fritzing sketch Untitled Sketch (saved by Fritzing 0.9.3b)
breadboards: 1

parts:
  LED1 = LED - 5mm [color="Red (633nm)" package="5 mm [THT]"]
  LED2 = LED - 5mm [color="Green (565nm)" package="5 mm [THT]"]
  R1 = Resistor [tolerance=±5% resistance=220 package=THT]
  Q1 = NPN-Transistor [package="TO92 [THT]"]
  R2 = Resistor [tolerance=±5% resistance=24k package=THT]
  R3 = Resistor [tolerance=±5% resistance=220 package=THT]
  Rele = OMRON PCB Power Relay – G5LE [part_number=5V package=THT]
  Keypad4x1 = Keypad Membran 4x4
  Part1 = Arduino Uno (Rev3)
  U1 = DIODE-ZENER [package=diode-zener]

nets:
  N1: LED1.cathode, R3.Pin_0
  N2: LED1.anode, Rele.A
  N3: LED2.cathode, R1.Pin_0
  N4: LED2.anode, Rele.B
  N5: R1.Pin_1, Q1.E, R3.Pin_1, Part1.GND
  N6: Q1.C, Rele.COIL1, U1.C
  N7: R2.Pin_0, Part1.D11_PWM/MOSI
  N8: Rele.C, Rele.COIL2, Part1.5V, U1.A
  N9: Keypad4x1.Pin1, Part1.D9_PWM
  N10: Keypad4x1.Pin2, Part1.D8
  N11: Keypad4x1.Pin3, Part1.D7
  N12: Keypad4x1.Pin4, Part1.D6_PWM
  N13: Keypad4x1.Pin5, Part1.D5_PWM
  N14: Keypad4x1.Pin6, Part1.D4
  N15: Keypad4x1.Pin7, Part1.D3_PWM
  N16: Keypad4x1.Pin8, Part1.D2

custom parts:
  Keypad Membran 4x4: Membrane Keypad 4x4 Matrix
